# Fritzing sketch Aufbau_Fritzing-DESKTOP-R0FJAJV (saved by Fritzing 0.9.9b)

parts:
  Bauteil1 = Adafruit PCA9685 PWM/Servo Breakout [part_number=815]
  Bauteil2 = Adafruit PCA9685 PWM/Servo Breakout [part_number=815]
  Bauteil3 = Arduino Mega 2560 (Rev3)  # not connected
  Brushless_motor1 = Brushless Motor
  ESC1 = ESC 30A
  U1 = LIPO-11.1V-3 Cells [package=Li-Po-2200]  # not connected
  Brushless_motor2 = Brushless Motor
  Brushless_motor3 = Brushless Motor
  Brushless_motor4 = Brushless Motor
  ESC2 = ESC 30A
  J15 = Basic Servo  # not connected
  J18 = Basic Servo  # not connected
  J20 = Basic Servo  # not connected
  J21 = Basic Servo  # not connected
  J22 = Basic Servo  # not connected
  J23 = Basic Servo  # not connected
  J24 = Basic Servo  # not connected
  J25 = Basic Servo  # not connected
  J26 = Basic Servo  # not connected
  J27 = Basic Servo  # not connected
  J28 = Basic Servo  # not connected
  J29 = Basic Servo  # not connected
  J30 = Basic Servo  # not connected
  J31 = Basic Servo  # not connected
  J32 = Basic Servo  # not connected
  J33 = Basic Servo  # not connected
  J34 = Basic Servo  # not connected
  J35 = Basic Servo  # not connected

nets:
  N1: Bauteil1.5.0V, Bauteil2.5.0V
  VCC: Bauteil1.VCC, Bauteil2.VCC
  N2: Bauteil1.SDA, Bauteil2.SDA
  N3: Bauteil1.SCL, Bauteil2.SCL
  N4: Bauteil1.OE, Bauteil2.OE
  GND: Bauteil1.GND, Bauteil2.GND
  N5: Brushless_motor1.A, ESC1.A, Brushless_motor2.A
  N6: Brushless_motor1.B, ESC1.B, Brushless_motor2.B
  N7: Brushless_motor1.C, ESC1.C, Brushless_motor2.C
  N8: Brushless_motor3.A, Brushless_motor4.A, ESC2.A
  N9: Brushless_motor3.B, Brushless_motor4.B, ESC2.B
  N10: Brushless_motor3.C, Brushless_motor4.C, ESC2.C

custom parts:
  Adafruit PCA9685 PWM/Servo Breakout: Using only two pins, control 16 free-running PWM outputs! I2C-controlled PWM driver with a built in clock. Unlike the TLC5940 family, you do not need to continuously send it signal tying up your microcontroller, its completely free running! 5V compliant, which means you can control it from a 3.3V microcontroller and still safely drive up to 6V outputs (this is good for when you want to control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
  Brushless Motor: A standard Brushless DC motor
  ESC 30A: Electronic Speed Controller - 30A
  LIPO-11.1V-3 Cells: Li-Po Battery-11.1V-3Cells-2200mAh
