# Fritzing sketch Parallelschaltung 2 Motoren (saved by Fritzing 0.9.9b)

parts:
  Brushless_motor1 = Brushless Motor
  Brushless_motor2 = Brushless Motor
  ESC1 = ESC 30A

nets:
  N1: Brushless_motor1.A, Brushless_motor2.A, ESC1.C
  N2: Brushless_motor1.B, Brushless_motor2.B, ESC1.B
  N3: Brushless_motor1.C, Brushless_motor2.C, ESC1.A

custom parts:
  Brushless Motor: A standard Brushless DC motor
  ESC 30A: Electronic Speed Controller - 30A
