# Fritzing sketch Spinnenroboter_Schaltplan (saved by Fritzing 0.9.9b)

parts:
  Arduino_Mega = Arduino Mega 2560 (Rev3)
  Brushlessmotor_links_hinten = Brushless Motor
  Brushlessmotor_links_vorne = Brushless Motor
  ESC_links = ESC 30A
  SVL1 = Basic Servo
  SVL3 = Basic Servo
  SML2 = Basic Servo
  SML1 = Basic Servo
  SHL1 = Basic Servo
  SHL2 = Basic Servo
  SML3 = Basic Servo
  SHL3 = Basic Servo
  Servoboard_links = Adafruit PCA9685 PWM/Servo Breakout [part_number=815]
  SHR3 = Basic Servo
  SMR3 = Basic Servo
  SVR3 = Basic Servo
  SHR1 = Basic Servo
  SVR1 = Basic Servo
  SHR2 = Basic Servo
  SMR2 = Basic Servo
  SVR2 = Basic Servo
  Brushlessmotor_rechts_hinten = Brushless Motor
  Brushlessmotor_rechts_vorne = Brushless Motor
  ESC_rechts = ESC 30A
  Servoboard_rechts = Adafruit PCA9685 PWM/Servo Breakout [part_number=815]
  Akku = LIPO-11.1V-3 Cells [package=Li-Po-2200]
  SVL2 = Basic Servo
  SMR1 = Basic Servo

nets (from the schematic view):
  N1: Arduino_Mega.D21/SCL, Arduino_Mega.SCL, Servoboard_links.SCL, Servoboard_rechts.SCL
  N2: Arduino_Mega.D20/SDA, Arduino_Mega.SDA, Servoboard_links.SDA, Servoboard_rechts.SDA
  VCC: Arduino_Mega.IOREF, Servoboard_links.VCC, Servoboard_rechts.VCC
  GND: Arduino_Mega.GND, ESC_links.GND#4, SVL1.gnd, SVL3.gnd, SML2.gnd, SML1.gnd, SHL1.gnd, SHL2.gnd, SML3.gnd, SHL3.gnd, Servoboard_links.GND, SHR3.gnd, SMR3.gnd, SVR3.gnd, SHR1.gnd, SVR1.gnd, SHR2.gnd, SMR2.gnd, SVR2.gnd, ESC_rechts.GND#4, Servoboard_rechts.GND, SVL2.gnd, SMR1.gnd
  N3: Brushlessmotor_links_hinten.A, Brushlessmotor_links_vorne.A, ESC_links.A
  N4: Brushlessmotor_links_hinten.B, Brushlessmotor_links_vorne.B, ESC_links.B
  N5: Brushlessmotor_links_hinten.C, Brushlessmotor_links_vorne.C, ESC_links.C
  N6: ESC_links.GND#5, ESC_rechts.GND#5, Akku.-
  N7: ESC_links.V+, ESC_rechts.V+, Akku.+
  N8: ESC_links.In, Servoboard_links.PWM12
  VCC_2: SVL1.vcc, SVL3.vcc, SML2.vcc, SML1.vcc, SHL1.vcc, SHL2.vcc, SML3.vcc, SHL3.vcc, Servoboard_links.5.0V, SHR3.vcc, SMR3.vcc, SVR3.vcc, SHR1.vcc, SVR1.vcc, SHR2.vcc, SMR2.vcc, SVR2.vcc, Servoboard_rechts.5.0V, SVL2.vcc, SMR1.vcc
  N9: SVL1.pulse, Servoboard_links.PWM0
  N10: SVL3.pulse, Servoboard_links.PWM2
  N11: SML2.pulse, Servoboard_links.PWM5
  N12: SML1.pulse, Servoboard_links.PWM4
  N13: SHL1.pulse, Servoboard_links.PWM8
  N14: SHL2.pulse, Servoboard_links.PWM9
  N15: SML3.pulse, Servoboard_links.PWM6
  N16: SHL3.pulse, Servoboard_links.PWM10
  N17: Servoboard_links.PWM1, SVL2.pulse
  N18: Servoboard_links.OE, Servoboard_rechts.OE
  N19: SHR3.pulse, Servoboard_rechts.PWM10
  N20: SMR3.pulse, Servoboard_rechts.PWM6
  N21: SVR3.pulse, Servoboard_rechts.PWM2
  N22: SHR1.pulse, Servoboard_rechts.PWM8
  N23: SVR1.pulse, Servoboard_rechts.PWM0
  N24: SHR2.pulse, Servoboard_rechts.PWM9
  N25: SMR2.pulse, Servoboard_rechts.PWM5
  N26: SVR2.pulse, Servoboard_rechts.PWM1
  N27: Brushlessmotor_rechts_hinten.A, Brushlessmotor_rechts_vorne.A, ESC_rechts.A
  N28: Brushlessmotor_rechts_hinten.B, Brushlessmotor_rechts_vorne.B, ESC_rechts.B
  N29: Brushlessmotor_rechts_hinten.C, Brushlessmotor_rechts_vorne.C, ESC_rechts.C
  N30: ESC_rechts.In, Servoboard_rechts.PWM12
  N31: Servoboard_rechts.PWM4, SMR1.pulse

notes:
  Bein vorne links
  Bein hinten links
  Bein mitte links
  Lenkservo
  Hubservo
  Stellservo (Arm)
  Motor links vorne
  Motor links hinten
  Bein vorne rechts
  Bein mitte rechts
  Bein hinten rechts
  Motor links rechts
  5V Spannungsversorung
  7,4V- 11,1V Spannungsversorung
  6V Spannungsversorung

custom parts:
  Brushless Motor: A standard Brushless DC motor
  ESC 30A: Electronic Speed Controller - 30A
  Adafruit PCA9685 PWM/Servo Breakout: Using only two pins, control 16 free-running PWM outputs! I2C-controlled PWM driver with a built in clock. Unlike the TLC5940 family, you do not need to continuously send it signal tying up your microcontroller, its completely free running! 5V compliant, which means you can control it from a 3.3V microcontroller and still safely drive up to 6V outputs (this is good for when you want to control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
  LIPO-11.1V-3 Cells: Li-Po Battery-11.1V-3Cells-2200mAh
